# Fritzing sketch AirQualityMonitorProject_v.1.0 (saved by Fritzing 0.9.3b)
circuit board: 12cm x 6.5cm
circuit board: 10.61cm x 6cm
breadboards: 1

parts:
  Humidity_sensor = Humidity and Temperature Sensor RHT03
  TD-er1 = MH-Z19 CO2 sensor [part_number=MH-Z19]
  IC1_(flash) = 24LC01 [package=THT]
  5V_Converter = female pin header, 3 pins [form="♀ (female)"]
  + = female pin header, 2 pins [form="♀ (female)"]
  GAS_sensor = Humidity and Temperature Sensor RHT03
  Nano = Arduino Nano (Rev3.0)
  R1 = Resistor [tolerance=±5% resistance=6.8 package=THT]  # not connected
  R2 = Resistor [tolerance=±5% resistance=6.8 package=THT]
  S1 = SWITCH-MOMENTARY-2 [package=tactile_switch_smd-2]
  R3 = Resistor [tolerance=±5% resistance=20 package=THT]
  R4 = Resistor [tolerance=±5% resistance=4.7 package=THT]
  LED_SCREEN1 = female pin header, 8 pins [form="♀ (female)"]
  SG1 = Buzzer 12mm [package=buzzer-ccv-kit]
  C1 = Electrolytic Capacitor [capacitance=1µF package="100 mil [THT, electrolytic]"]
  R5 = Trimmer Potentiometer [maximum_resistance=10kΩ package=THT]

nets (from the pcb view):
  VCC: Humidity_sensor.Vcc, TD-er1.Vin, IC1_(flash).SDA_-_I2C_Data, 5V_Converter.pin1, GAS_sensor.Vcc, Nano.VIN, R2.Pin_1, R4.Pin_0, LED_SCREEN1.pin8, C1.+
  N1: Humidity_sensor.Data-signal, IC1_(flash).+V, Nano.A4
  N2: Humidity_sensor.GND_1, GAS_sensor.Data-signal
  N3: TD-er1.RX, Nano.A1
  N4: TD-er1.TX, Nano.A0
  N5: IC1_(flash).A0, IC1_(flash).SCL_-_I2C_Clock, SG1.2
  N6: IC1_(flash).WP_-_Write_Protect, Nano.A5
  N7: 5V_Converter.pin2, +.pin1, Nano.GND, LED_SCREEN1.pin7, C1.-
  N8: 5V_Converter.pin3, +.pin2
  N9: GAS_sensor.GND_2, Nano.A7
  N10: Nano.D2, LED_SCREEN1.pin6
  N11: Nano.D3, LED_SCREEN1.pin5
  N12: Nano.D4, LED_SCREEN1.pin4
  N13: Nano.D5, S1.2, R3.Pin_1
  N14: Nano.D11/MOSI, LED_SCREEN1.pin3
  N15: Nano.A2, SG1.1
  N16: Nano.D13/SCK, LED_SCREEN1.pin2
  N17: S1.1, R4.Pin_1
  N18: LED_SCREEN1.pin1, R5.leg1

notes:
  Front Pannel
  I2C Bus
