# Fritzing sketch CO2 (saved by Fritzing 0.9.3b)
circuit board: 4.3cm x 5.8cm
circuit board: 5.99333cm x 10.6119cm
circuit board: 12cm x 6.5cm
breadboards: 1

parts:
  Nano = Arduino Nano (Rev3.0)
  Humidity_sensor = Humidity and Temperature Sensor RHT03
  Temp/Pres/Sensor = Altitude/Pressure Sensor - MPL3115A2 Breakout [part_number=SEN-11084]
  LED1 = LED - 5mm [color="Red (633nm)" package="5 mm [THT]"]  # not connected
  TD-er1 = MH-Z19 CO2 sensor [part_number=MH-Z19]
  Dust_Sensor = Grove Dust Sensor
  U1_(WI-FI) = ESP8266 WiFi Module [part_number=ESP8266]
  LED_Screen = OLED 0.96" 128x64 I2C SSD1306 (GND/VCC)  # not connected
  IC1_(flash) = 24LC01 [package=THT]
  LED_SCREEN = female pin header, 4 pins [form="♀ (female)"]
  5V_Converter = female pin header, 3 pins [form="♀ (female)"]
  + = female pin header, 2 pins [form="♀ (female)"]
  part = TXB0108 8-channel Bi-directional Logic Level Converter
  LED_SCREEN1 = female pin header, 8 pins [form="♀ (female)"]

nets (from the pcb view):
  GND: Nano.GND, TD-er1.GND, U1_(WI-FI).GND, LED_SCREEN.pin1, LED_SCREEN.pin2, 5V_Converter.pin2, +.pin1
  N1: Nano.D2, part.B8
  N2: Nano.D3, part.B7
  N3: Nano.D4, part.B6
  N4: Nano.D5, part.B5
  N5: Nano.D6, part.B4
  N6: Nano.D7, part.B3
  N7: Nano.D8, part.B2
  N8: Nano.D9, part.B1
  VCC: Nano.VIN, Humidity_sensor.Vcc, Temp/Pres/Sensor.VCC, TD-er1.Vin, Dust_Sensor.VCC, 5V_Converter.pin1, part.VCCB
  N9: Nano.A5, Humidity_sensor.GND_2, Temp/Pres/Sensor.SCL, IC1_(flash).SCL_-_I2C_Clock, LED_SCREEN.pin3
  N10: Nano.A4, Humidity_sensor.Data-signal, IC1_(flash).SDA_-_I2C_Data, LED_SCREEN.pin4
  N11: Nano.A1, TD-er1.RX
  N12: Nano.A0, TD-er1.TX
  3V3: Nano.3V3, U1_(WI-FI).VCC, part.VCCA
  GND_2: Humidity_sensor.GND_1, Temp/Pres/Sensor.GND, Dust_Sensor.GND, part.GND
  N13: IC1_(flash).0V, IC1_(flash).WP_-_Write_Protect
  N14: 5V_Converter.pin3, +.pin2
  N15: part.A8, LED_SCREEN1.pin1
  N16: part.A7, LED_SCREEN1.pin2
  N17: part.A6, LED_SCREEN1.pin3
  N18: part.A5, LED_SCREEN1.pin4
  N19: part.A4, LED_SCREEN1.pin5
  N20: part.A3, LED_SCREEN1.pin6
  N21: part.A2, LED_SCREEN1.pin7
  N22: part.A1, LED_SCREEN1.pin8

notes:
  Dust sensor
  Front Pannel

custom parts:
  Grove Dust Sensor: PPD42 Grove Dust Sensor
  OLED 0.96" 128x64 I2C SSD1306 (GND/VCC): OLED 0.96" 128x64 I2C SSD1306 Pinout: GND/VCC/SCL/SDA
  TXB0108 8-channel Bi-directional Logic Level Converter: Because the Arduino (and Basic Stamp) are 5V devices, and most modern sensors, displays, flash cards and modes are 3.3V-only, many makers find that they need to perform level shifting/conversion to protect the 3.3V device from 5V. Although one can use resistors to make a divider, for high speed transfers, the resistors can add a lot of slew and cause havoc that is tough to debug. For that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
